# Fritzing sketch Pi Dice (saved by Fritzing 0.9.2b)
breadboards: 1

parts:
  Raspberry_Pi1 = Raspberry Pi 2
  R1 = Resistor [tolerance=±5% resistance=220 package=THT]
  LED1 = LED - 5mm [color="Red (633nm)" package="5 mm [THT]"]
  S1 = Pushbutton [package="[THT]"]
  LED2 = LED - 5mm [color="Red (633nm)" package="5 mm [THT]"]
  LED3 = LED - 5mm [color="Red (633nm)" package="5 mm [THT]"]
  LED4 = LED - 5mm [color="Red (633nm)" package="5 mm [THT]"]
  LED5 = LED - 5mm [color="Red (633nm)" package="5 mm [THT]"]
  LED6 = LED - 5mm [color="Red (633nm)" package="5 mm [THT]"]
  R2 = Resistor [tolerance=±5% resistance=220 package=THT]
  R3 = Resistor [tolerance=±5% resistance=220 package=THT]
  R4 = Resistor [tolerance=±5% resistance=220 package=THT]
  R5 = Resistor [tolerance=±5% resistance=220 package=THT]
  R6 = Resistor [tolerance=±5% resistance=220 package=THT]

nets:
  N1: Raspberry_Pi1.GPIO21, S1.Pin_1, S1.Pin_2
  N2: Raspberry_Pi1.GPIO25, R6.Pin_0
  N3: Raspberry_Pi1.GPIO24, R5.Pin_0
  N4: Raspberry_Pi1.GPIO23, R4.Pin_0
  N5: Raspberry_Pi1.GPIO18, R3.Pin_0
  N6: Raspberry_Pi1.GPIO15, R2.Pin_0
  N7: Raspberry_Pi1.GPIO14, R1.Pin_0
  N8: Raspberry_Pi1.GND, LED1.cathode, S1.Pin_3, S1.Pin_4, LED2.cathode, LED3.cathode, LED4.cathode, LED5.cathode, LED6.cathode
  N9: R1.Pin_1, LED1.anode
  N10: LED2.anode, R4.Pin_1
  N11: LED3.anode, R2.Pin_1
  N12: LED4.anode, R5.Pin_1
  N13: LED5.anode, R3.Pin_1
  N14: LED6.anode, R6.Pin_1
